# Fritzing sketch ESP06 (saved by Fritzing 0.9.3b)
circuit board: 3.04235cm x 2.22533cm
breadboards: 1

parts:
  IC2 = Voltage Regulator LM1117 [part_number="AMS1117 33" package=sot223]
  R1 = Resistor [tolerance=±5% resistance=3.3k package="1206 [SMD]"]
  R2 = Resistor [tolerance=±5% resistance=10k package="1206 [SMD]"]
  R3 = Resistor [tolerance=±5% resistance=4.7k package="1206 [SMD]"]
  DISTANCE = female pin header, 4 pins [form="♀ (female)"]
  C2 = SMD Capacitor [package=1206]
  C1 = SMD Capacitor [package=1206]
  Espessif_Serial_Wifi_Modul_1 = ESP8266 ESP01 [part_number=ESP8266 package=THT]
  DS18 = female pin header, 3 pins [form="♀ (female)"]
  U1 = USB Connectors [package=usb-microb]

nets:
  GND: IC2.ADJ, R2.Pin_0, DISTANCE.pin4, C2.2, C1.2, Espessif_Serial_Wifi_Modul_1.GND, DS18.pin3, U1.GND
  3.3V: IC2.OUT, R1.Pin_1, C2.1, Espessif_Serial_Wifi_Modul_1.VCC, Espessif_Serial_Wifi_Modul_1.GPIO16, Espessif_Serial_Wifi_Modul_1.CH_PD, DS18.pin1
  5V: IC2.IN, DISTANCE.pin1, C1.1, U1.VBUS
  ONEWIRE: R1.Pin_0, Espessif_Serial_Wifi_Modul_1.GPIO00, Espessif_Serial_Wifi_Modul_1.GPIO02, DS18.pin2
  N1: R2.Pin_1, R3.Pin_1, Espessif_Serial_Wifi_Modul_1.RXD
  ECHO: R3.Pin_0, DISTANCE.pin3
  TRIG: DISTANCE.pin2, Espessif_Serial_Wifi_Modul_1.TXD

notes:
  3.3V
  GND
  5V

custom parts:
  SMD Capacitor: Capacitor Standard 0603 ceramic capacitor, and 0.1 leaded capacitor.
  ESP8266 ESP01: Generic WiFi Module based on the ESP8266 with onboard PCB antenna and UART communications
